# Fritzing sketch ShuttleStride_circuit-diagram (saved by Fritzing 0.9.3b)

parts:
  Part1 = BluePill
  M1 = fc-51 [package=THT]
  Part2 = NRF24L01+ Breakout Board
  LED3 = LEDs [package=led10mm]
  U1 = BATTERY-2 [package=battery-aa]
  U2 = BATTERY-2 [package=battery-aa]
  LED6 = LEDs [package=led10mm]
  LED2 = LEDs [package=led10mm]

nets:
  N1: Part1.A4, Part2.CS
  N2: Part1.A5, Part2.SCK
  N3: Part1.A6, Part2.MISO
  N4: Part1.A7, Part2.MOSI
  N5: Part1.B0, Part2.CE
  N6: Part1.B11, LED2.A
  3V3: Part1.3V3, Part2.VCC
  GND2: Part1.GND2, Part2.GND, LED2.C
  N7: Part1.3V31, U2.+1
  N8: Part1.GND3, M1.pin2, LED3.C, U1.-1, LED6.C
  N9: Part1.5V, M1.pin3
  N10: Part1.B9, M1.pin1
  N11: Part1.B8, LED3.A
  N12: Part1.B7, LED6.A
  N13: U1.+1, U2.-1
